// Logisim project multiplicador.circ as structural Verilog: 2 circuits, main circuit main
module main (
  input  [7:0] in_1,
  input  [7:0] in_2
);
endmodule

// mULTIPLICADOR
module multiplicador (
  input  [7:0] A,
  input  [7:0] B,
  output [7:0] out_3,
  output [7:0] out_4
);

  wire clock_1_out, comparator_1_eq, comparator_1_gt, comparator_1_lt, not_1_out;
  wire [7:0] adder_1_out, controlled_buffer_1_out;

  // Probe on A
  // Probe on B
  Clock clock_1 (.out(clock_1_out));
  // Probe on out_4
  Counter counter_1 (.Q(out_4), .clk(clock_1_out), .clr(comparator_1_gt));  // open: load, D, count, carry
  assign controlled_buffer_1_out = comparator_1_lt ? out_3 : 8'bz;  // Controlled_Buffer controlled_buffer_1
  Adder adder_1 (.a(A), .b(controlled_buffer_1_out), .out(adder_1_out));  // open: cin, cout
  Comparator comparator_1 (.a(out_4), .b(B), .gt(comparator_1_gt), .eq(comparator_1_eq), .lt(comparator_1_lt));
  not not_1 (not_1_out, comparator_1_eq);
  // Probe on adder_1_out
  Register register_1 (.D(adder_1_out), .en(not_1_out), .Q(out_3), .clk(clock_1_out), .clr(comparator_1_gt));
endmodule
