// Logisim project contador descescente 15 até 10.circ as structural Verilog: 1 circuit, main circuit main
module main (
);

  wire and_1_out, clock_1_out;
  wire [3:0] t_ff_1_q;

  Clock clock_1 (.out(clock_1_out));
  and and_1 (and_1_out, t_ff_1_q[0], ~t_ff_1_q[1], ~t_ff_1_q[2], t_ff_1_q[3]);  // AND_Gate
  T_Flip_Flop t_ff_1 (.clk(clock_1_out), .T(clock_1_out), .Q(t_ff_1_q[0]), .reset(and_1_out));  // open: Qn, preset, en
  // Probe on t_ff_1_q
  T_Flip_Flop t_ff_2 (.clk(t_ff_1_q[0]), .T(clock_1_out), .Q(t_ff_1_q[1]), .reset(and_1_out));  // open: Qn, preset, en
  T_Flip_Flop t_ff_3 (.clk(t_ff_1_q[1]), .T(clock_1_out), .Q(t_ff_1_q[2]), .reset(and_1_out));  // open: Qn, preset, en
  T_Flip_Flop t_ff_4 (.clk(t_ff_1_q[2]), .T(clock_1_out), .Q(t_ff_1_q[3]), .reset(and_1_out));  // open: Qn, preset, en
endmodule
