// Logisim project contador_crescente_deecrescente.circ as structural Verilog: 1 circuit, main circuit main
module main (
  output out_1,
  output out_2,
  output out_3,
  output out_4,
  output out_5,
  output out_6,
  output out_7,
  output out_8
);

  wire clock_1_out, clock_2_out;

  Clock clock_1 (.out(clock_1_out));
  Clock clock_2 (.out(clock_2_out));
  T_Flip_Flop #(.trigger("falling")) t_ff_1 (.clk(clock_1_out), .T(1'b1), .Q(out_1));  // open: Qn, preset, reset, en
  T_Flip_Flop #(.trigger("falling")) t_ff_2 (.clk(out_1), .T(1'b1), .Q(out_2));  // open: Qn, preset, reset, en
  T_Flip_Flop t_ff_3 (.clk(clock_2_out), .T(1'b1), .Q(out_5));  // open: Qn, preset, reset, en
  T_Flip_Flop #(.trigger("falling")) t_ff_4 (.clk(out_2), .T(1'b1), .Q(out_3));  // open: Qn, preset, reset, en
  T_Flip_Flop t_ff_5 (.clk(out_5), .T(1'b1), .Q(out_6));  // open: Qn, preset, reset, en
  T_Flip_Flop #(.trigger("falling")) t_ff_6 (.clk(out_3), .T(1'b1), .Q(out_4));  // open: Qn, preset, reset, en
  T_Flip_Flop t_ff_7 (.clk(out_6), .T(1'b1), .Q(out_7));  // open: Qn, preset, reset, en
  T_Flip_Flop t_ff_8 (.clk(out_7), .T(1'b1), .Q(out_8));  // open: Qn, preset, reset, en

  // Notes on the sheet:
  //   esse outro aqui vai do maior pro menor (é um temporizador) as coisas acontecem quando varia de 0 pra 1
  //   nesse contador aqui quando clock varia de 1 pra 0 é que as coisas acontecem
endmodule
