// Logisim project código johnson.circ as structural Verilog: 1 circuit, main circuit main
module main (
  output [3:0] out_1
);

  wire clock_1_out, not_1_out;

  Clock clock_1 (.out(clock_1_out));
  D_Flip_Flop #(.trigger("falling")) d_ff_1 (
    .clk(clock_1_out), .D(not_1_out), .Q(out_1[0]));  // open: Qn, preset, en, reset
  D_Flip_Flop #(.trigger("falling")) d_ff_2 (
    .clk(clock_1_out), .D(out_1[0]), .Q(out_1[1]));  // open: Qn, preset, en, reset
  D_Flip_Flop #(.trigger("falling")) d_ff_3 (
    .clk(clock_1_out), .D(out_1[1]), .Q(out_1[2]));  // open: Qn, preset, en, reset
  not not_1 (not_1_out, out_1[3]);
  D_Flip_Flop #(.trigger("falling")) d_ff_4 (
    .clk(clock_1_out), .D(out_1[2]), .Q(out_1[3]));  // open: Qn, preset, en, reset
endmodule
