// Logisim project deslocador a direita.circ as structural Verilog: 1 circuit, main circuit main
module main (
  input  in_1,
  input  in_2,
  output out_3,
  output out_4,
  output out_5,
  output out_6
);

  wire clock_1_out;

  Clock clock_1 (.out(clock_1_out));
  Register #(.width(1)) register_1 (.D(1'b0), .en(in_2), .Q(out_3), .clk(clock_1_out), .clr(in_1));
  Register #(.width(1)) register_2 (.D(out_3), .en(in_2), .Q(out_4), .clk(clock_1_out), .clr(in_1));
  Register #(.width(1)) register_3 (.D(out_4), .en(in_2), .Q(out_5), .clk(clock_1_out), .clr(in_1));
  Register #(.width(1)) register_4 (.D(out_5), .en(in_2), .Q(out_6), .clk(clock_1_out), .clr(in_1));
endmodule
