// Logisim project registrador com JK.circ as structural Verilog: 2 circuits, main circuit main
module main (
);

  registrador_4 registrador_4_1 ();  // open: in_1, in_2, in_3, in_4, out_5
endmodule

module registrador_4 (
  input  in_1,
  input  in_2,
  input  in_3,
  input  in_4,
  output [3:0] out_5
);

  wire clock_1_out, not_1_out, not_2_out, not_3_out, not_4_out, undriven, undriven_2;

  not not_1 (not_1_out, in_2);
  not not_2 (not_2_out, in_3);
  J_K_Flip_Flop j_k_ff_1 (
    .J(in_1), .clk(clock_1_out), .K(not_3_out), .Q(out_5[0]), .en(undriven));  // open: Qn, preset, reset
  not not_3 (not_3_out, in_1);
  J_K_Flip_Flop j_k_ff_2 (
    .J(in_2), .clk(clock_1_out), .K(not_1_out), .Q(out_5[1]), .en(undriven_2), .reset(undriven_2));  // open: Qn, preset
  J_K_Flip_Flop j_k_ff_3 (.J(in_3), .clk(clock_1_out), .K(not_2_out), .Q(out_5[2]));  // open: Qn, preset, en, reset
  J_K_Flip_Flop j_k_ff_4 (.J(in_4), .clk(clock_1_out), .K(not_4_out), .Q(out_5[3]));  // open: Qn, preset, en, reset
  not not_4 (not_4_out, in_4);
  Clock clock_1 (.out(clock_1_out));
endmodule
