// Logisim project registrador de deslocamento.circ as structural Verilog: 1 circuit, main circuit main
module main (
  input  in_1,
  input  in_2
);

  wire clock_1_out;
  wire [3:0] d_ff_4_q;

  Clock clock_1 (.out(clock_1_out));
  D_Flip_Flop d_ff_1 (.clk(clock_1_out), .D(in_1), .Q(d_ff_4_q[3]), .en(in_2));  // open: Qn, preset, reset
  // Probe on d_ff_4_q
  D_Flip_Flop d_ff_2 (.clk(clock_1_out), .D(d_ff_4_q[3]), .Q(d_ff_4_q[2]), .en(in_2));  // open: Qn, preset, reset
  D_Flip_Flop d_ff_3 (.clk(clock_1_out), .D(d_ff_4_q[2]), .Q(d_ff_4_q[1]), .en(in_2));  // open: Qn, preset, reset
  D_Flip_Flop d_ff_4 (.clk(clock_1_out), .D(d_ff_4_q[1]), .Q(d_ff_4_q[0]));  // open: Qn, preset, en, reset
endmodule
