// Logisim project multiplexador.circ as structural Verilog: 1 circuit, main circuit main
module main (
  input  in_1,
  input  in_2,
  input  in_3,
  input  in_4,
  input  in_5,
  input  in_6,
  output out_7
);

  wire and_1_out, and_2_out, and_3_out, and_4_out;

  assign out_7 = and_1_out ? in_1 : 1'bz;  // Controlled_Buffer controlled_buffer_1
  and and_1 (and_1_out, ~in_5, ~in_6);  // AND_Gate
  assign out_7 = and_2_out ? in_2 : 1'bz;  // Controlled_Buffer controlled_buffer_2
  and and_2 (and_2_out, ~in_5, in_6);  // AND_Gate
  assign out_7 = and_3_out ? in_3 : 1'bz;  // Controlled_Buffer controlled_buffer_3
  and and_3 (and_3_out, in_5, ~in_6);  // AND_Gate
  assign out_7 = and_4_out ? in_4 : 1'bz;  // Controlled_Buffer controlled_buffer_4
  and and_4 (and_4_out, in_5, in_6);
endmodule
